// Logisim project Lab2_digital_logic.circ as structural Verilog: 6 circuits, main circuit main
module main (
  input  NAND_Not,
  input  NAND_And,
  input  NAND_Or,
  input  in_4,
  input  in_5,
  input  in_6,
  input  in_7,
  input  Input_A,
  input  Input_B,
  input  Carry_In,
  input  in_11,
  input  in_12,
  input  in_13,
  input  in_14,
  input  in_15,
  input  in_16,
  input  in_17,
  input  in_18,
  input  in_19,
  input  in_20,
  input  in_21,
  input  in_22,
  input  in_23,
  input  in_24,
  input  in_25,
  input  in_26,
  input  [7:0] in_27,
  input  [7:0] in_28,
  input  [2:0] in_29,
  output out_30,
  output out_31,
  output out_32,
  output out_33,
  output Sum,
  output Carry_Out,
  output out_36,
  output out_37,
  output out_38,
  output out_39,
  output out_40,
  output out_41,
  output out_42,
  output [7:0] out_43
);

  wire adder_1_out, and_1_out, and_2_out, and_3_out, and_4_out, and_6_out, and_7_out, and_8_out, and_9_out,
       and_10_out, and_11_out, and_12_out, and_13_out, comparator_1_lt, multiplexer_1_out, multiplexer_2_out,
       nand_2_out, not_1_out, not_2_out, not_3_out, not_4_out, not_6_out, or_1_out, or_2_out, or_4_out,
       or_5_out, or_6_out, xor_1_out, xor_2_out, xor_6_out, xor_8_out, xor_10_out;
  wire [7:0] adder_2_out, bit_extender_1_out, divider_1_out, multiplier_1_out, subtractor_1_out, xor_5_out;

  not not_1 (not_1_out, in_4);
  not not_2 (not_2_out, in_5);
  and and_1 (and_1_out, Input_A, Input_B);
  xor xor_1 (xor_1_out, in_11, in_15);
  and and_2 (and_2_out, in_11, in_15);
  Multiplexer multiplexer_1 (.in0(in_20), .in1(not_3_out), .out(multiplexer_1_out), .sel(in_21));
  not not_3 (not_3_out, in_20);
  Multiplexer multiplexer_2 (.in0(in_22), .in1(not_4_out), .out(multiplexer_2_out), .sel(in_24));
  not not_4 (not_4_out, in_22);
  nand nand_1 (out_30, NAND_Not, NAND_Not);
  nand nand_2 (nand_2_out, NAND_And, NAND_Or);
  not not_5 (out_31, nand_2_out);
  nand nand_3 (out_32, not_1_out, not_2_out);
  and and_3 (and_3_out, in_6, in_7);
  not not_6 (not_6_out, and_3_out);
  or or_1 (or_1_out, in_6, in_7);
  xor xor_2 (xor_2_out, Input_A, Input_B);
  and and_4 (and_4_out, multiplexer_1_out, multiplexer_2_out);
  or or_2 (or_2_out, multiplexer_1_out, multiplexer_2_out);
  Adder #(.width(1)) adder_1 (
    .a(multiplexer_1_out), .b(multiplexer_2_out), .out(adder_1_out), .cin(in_25), .cout(out_42));
  and and_5 (out_33, not_6_out, or_1_out);
  xor xor_3 (Sum, xor_2_out, Carry_In);
  and and_6 (and_6_out, xor_2_out, Carry_In);
  xor xor_4 (out_36, xor_1_out, in_19);
  and and_7 (and_7_out, xor_1_out, in_19);
  Multiplexer #(.select(2)) multiplexer_3 (
    .in0(and_4_out), .in1(or_2_out), .in2(adder_1_out), .out(out_41), .sel({in_26, in_23}));  // open: in3
  Adder adder_2 (.a(in_27), .b(in_28), .out(adder_2_out));  // open: cin, cout
  Subtractor subtractor_1 (.a(in_27), .b(in_28), .out(subtractor_1_out));  // open: bin, bout
  Multiplier multiplier_1 (.a(in_27), .b(in_28), .out(multiplier_1_out));  // open: cin, cout
  Divider divider_1 (.a(in_27), .b(in_28), .out(divider_1_out));  // open: upper, rem
  assign xor_5_out = in_27 ^ in_28;  // XOR_Gate xor_5, 8 bits wide
  Comparator #(.mode("unsigned")) comparator_1 (.a(in_27), .b(in_28), .lt(comparator_1_lt));  // open: gt, eq
  or or_3 (Carry_Out, and_6_out, and_1_out);
  or or_4 (or_4_out, and_7_out, and_2_out);
  assign bit_extender_1_out = {{7{1'b0}}, comparator_1_lt};  // Bit_Extender bit_extender_1
  xor xor_6 (xor_6_out, in_12, in_16);
  and and_8 (and_8_out, in_12, in_16);
  Multiplexer #(.select(3), .width(8)) multiplexer_4 (
    .in0(adder_2_out), .in1(subtractor_1_out), .in2(multiplier_1_out), .in3(divider_1_out), .in4(xor_5_out),
    .in5(bit_extender_1_out), .out(out_43), .sel(in_29));  // open: in6, in7
  xor xor_7 (out_37, xor_6_out, or_4_out);
  and and_9 (and_9_out, xor_6_out, or_4_out);
  or or_5 (or_5_out, and_9_out, and_8_out);
  xor xor_8 (xor_8_out, in_13, in_17);
  and and_10 (and_10_out, in_13, in_17);
  xor xor_9 (out_38, xor_8_out, or_5_out);
  and and_11 (and_11_out, xor_8_out, or_5_out);
  or or_6 (or_6_out, and_11_out, and_10_out);
  xor xor_10 (xor_10_out, in_14, in_18);
  and and_12 (and_12_out, in_14, in_18);
  and and_13 (and_13_out, xor_10_out, or_6_out);
  xor xor_11 (out_39, xor_10_out, or_6_out);
  or or_7 (out_40, and_13_out, and_12_out);

  // Notes on the sheet:
  //   4-Bit Full Adder
  //   1-Bit Full Adder
endmodule

module NAND_universality (
  input  NAND_Not,
  input  NAND_And,
  input  NAND_Or,
  input  in_4,
  input  in_5,
  output out_6,
  output out_7,
  output out_8
);

  wire nand_2_out, not_1_out, not_2_out;

  not not_1 (not_1_out, in_4);
  not not_2 (not_2_out, in_5);
  nand nand_1 (out_6, NAND_Not, NAND_Not);
  nand nand_2 (nand_2_out, NAND_And, NAND_Or);
  not not_3 (out_7, nand_2_out);
  nand nand_3 (out_8, not_1_out, not_2_out);
endmodule

module XOR_lg (
  input  XOR,
  input  in_2,
  output out_3
);

  wire and_1_out, not_1_out, or_1_out;

  and and_1 (and_1_out, XOR, in_2);
  or or_1 (or_1_out, XOR, in_2);
  not not_1 (not_1_out, and_1_out);
  and and_2 (out_3, not_1_out, or_1_out);
endmodule

module Full_adder (
  input  Input_A,
  input  Input_B,
  input  Carry_In,
  input  in_4,
  input  in_5,
  input  in_6,
  input  in_7,
  input  in_8,
  input  in_9,
  input  in_10,
  input  in_11,
  input  in_12,
  output Sum,
  output Carry_Out,
  output out_15,
  output out_16,
  output out_17,
  output out_18,
  output out_19
);

  wire and_1_out, and_2_out, and_3_out, and_4_out, and_5_out, and_6_out, and_7_out, and_8_out, and_9_out,
       and_10_out, or_2_out, or_3_out, or_4_out, xor_1_out, xor_2_out, xor_5_out, xor_7_out, xor_9_out;

  xor xor_1 (xor_1_out, Input_A, Input_B);
  and and_1 (and_1_out, Input_A, Input_B);
  xor xor_2 (xor_2_out, in_4, in_8);
  and and_2 (and_2_out, in_4, in_8);
  xor xor_3 (Sum, xor_1_out, Carry_In);
  and and_3 (and_3_out, xor_1_out, Carry_In);
  xor xor_4 (out_15, xor_2_out, in_12);
  and and_4 (and_4_out, xor_2_out, in_12);
  or or_1 (Carry_Out, and_3_out, and_1_out);
  or or_2 (or_2_out, and_4_out, and_2_out);
  xor xor_5 (xor_5_out, in_5, in_9);
  and and_5 (and_5_out, in_5, in_9);
  xor xor_6 (out_16, xor_5_out, or_2_out);
  and and_6 (and_6_out, xor_5_out, or_2_out);
  or or_3 (or_3_out, and_6_out, and_5_out);
  xor xor_7 (xor_7_out, in_6, in_10);
  and and_7 (and_7_out, in_6, in_10);
  and and_8 (and_8_out, xor_7_out, or_3_out);
  xor xor_8 (out_17, xor_7_out, or_3_out);
  or or_4 (or_4_out, and_8_out, and_7_out);
  xor xor_9 (xor_9_out, in_7, in_11);
  and and_9 (and_9_out, in_7, in_11);
  xor xor_10 (out_18, xor_9_out, or_4_out);
  and and_10 (and_10_out, xor_9_out, or_4_out);
  or or_5 (out_19, and_10_out, and_9_out);

  // Notes on the sheet:
  //   1-Bit Full Adder
  //   4-Bit Full Adder
endmodule

module ALU_lg (
  input  ALU,
  input  in_2,
  input  in_3,
  input  in_4,
  input  in_5,
  input  in_6,
  input  in_7,
  output out_8,
  output out_9
);

  wire adder_1_out, and_1_out, multiplexer_1_out, multiplexer_2_out, not_1_out, not_2_out, or_1_out;

  Multiplexer multiplexer_1 (.in0(ALU), .in1(not_1_out), .out(multiplexer_1_out), .sel(in_2));
  not not_1 (not_1_out, ALU);
  Multiplexer multiplexer_2 (.in0(in_3), .in1(not_2_out), .out(multiplexer_2_out), .sel(in_5));
  not not_2 (not_2_out, in_3);
  Adder #(.width(1)) adder_1 (
    .a(multiplexer_1_out), .b(multiplexer_2_out), .out(adder_1_out), .cin(in_6), .cout(out_9));
  and and_1 (and_1_out, multiplexer_1_out, multiplexer_2_out);
  or or_1 (or_1_out, multiplexer_1_out, multiplexer_2_out);
  Multiplexer #(.select(2)) multiplexer_3 (
    .in0(and_1_out), .in1(or_1_out), .in2(adder_1_out), .out(out_8), .sel({in_7, in_4}));  // open: in3
endmodule

module MB_ALU (
  input  Multi_Bit_ALU,
  input  in_2,
  input  in_3,
  input  in_4,
  input  in_5,
  input  in_6,
  input  in_7,
  output out_8,
  output out_9
);

  wire adder_1_out, and_1_out, multiplexer_1_out, multiplexer_2_out, not_1_out, not_2_out, or_1_out;

  Multiplexer multiplexer_1 (.in0(Multi_Bit_ALU), .in1(not_1_out), .out(multiplexer_1_out), .sel(in_2));
  not not_1 (not_1_out, Multi_Bit_ALU);
  Multiplexer multiplexer_2 (.in0(in_3), .in1(not_2_out), .out(multiplexer_2_out), .sel(in_5));
  not not_2 (not_2_out, in_3);
  Adder #(.width(1)) adder_1 (
    .a(multiplexer_1_out), .b(multiplexer_2_out), .out(adder_1_out), .cin(in_6), .cout(out_9));
  and and_1 (and_1_out, multiplexer_1_out, multiplexer_2_out);
  or or_1 (or_1_out, multiplexer_1_out, multiplexer_2_out);
  Multiplexer #(.select(2)) multiplexer_3 (
    .in0(and_1_out), .in1(or_1_out), .in2(adder_1_out), .out(out_8), .sel({in_7, in_4}));  // open: in3
endmodule
